// Logisim project ex4.circ as structural Verilog: 5 circuits, main circuit RotRight
module RotRight (
  input  [15:0] INPUT0,
  input  [3:0] AMOUNT,
  output [15:0] OUTPUT0
);

  wire [15:0] rot1_1_out_3, rot2_1_out_3, rot4_1_out_3;

  rot1 rot1_1 (.in_1(INPUT0), .in_2(AMOUNT[0]), .out_3(rot1_1_out_3));
  rot2 rot2_1 (.in_1(rot1_1_out_3), .in_2(AMOUNT[1]), .out_3(rot2_1_out_3));
  rot4 rot4_1 (.in_1(rot2_1_out_3), .in_2(AMOUNT[2]), .out_3(rot4_1_out_3));
  rot8 rot8_1 (.in_1(rot4_1_out_3), .in_2(AMOUNT[3]), .out_3(OUTPUT0));
endmodule

module rot1 (
  input  [15:0] in_1,
  input  in_2,
  output [15:0] out_3
);

  Multiplexer #(.width(16)) multiplexer_1 (.in0(in_1), .in1({in_1[0], in_1[15:1]}), .out(out_3), .sel(in_2));
endmodule

module rot2 (
  input  [15:0] in_1,
  input  in_2,
  output [15:0] out_3
);

  Multiplexer #(.width(16)) multiplexer_1 (.in0(in_1), .in1({in_1[1:0], in_1[15:2]}), .out(out_3), .sel(in_2));
endmodule

module rot4 (
  input  [15:0] in_1,
  input  in_2,
  output [15:0] out_3
);

  Multiplexer #(.width(16)) multiplexer_1 (.in0(in_1), .in1({in_1[3:0], in_1[15:4]}), .out(out_3), .sel(in_2));
endmodule

module rot8 (
  input  [15:0] in_1,
  input  in_2,
  output [15:0] out_3
);

  Multiplexer #(.width(16)) multiplexer_1 (.in0(in_1), .in1({in_1[7:0], in_1[15:8]}), .out(out_3), .sel(in_2));
endmodule
