// Logisim project ex2.circ as structural Verilog: 1 circuit, main circuit compute_BrUn
module compute_BrUn (
  input  [31:0] INSTRUCTION,
  output BrUn
);

  wire comparator_1_eq, comparator_2_eq, comparator_3_eq, comparator_4_eq, comparator_5_eq, fin;
  wire [1:0] or_2_out;

  Comparator #(.mode("unsigned"), .width(7)) comparator_1 (
    .a(7'b1100011), .b(INSTRUCTION[6:0]), .eq(comparator_1_eq));  // open: gt, lt
  Multiplexer multiplexer_1 (.in0(1'b0), .in1(fin), .out(BrUn), .sel(comparator_1_eq));
  Comparator #(.mode("unsigned"), .width(3)) comparator_2 (
    .a(INSTRUCTION[14:12]), .b(3'b100), .eq(comparator_2_eq));  // open: gt, lt
  Comparator #(.width(3)) comparator_3 (.a(INSTRUCTION[14:12]), .b(3'b101), .eq(comparator_3_eq));  // open: gt, lt
  or or_1 (or_2_out[1], comparator_2_eq, comparator_3_eq);
  Comparator #(.mode("unsigned"), .width(3)) comparator_4 (
    .a(INSTRUCTION[14:12]), .b(3'b110), .eq(comparator_4_eq));  // open: gt, lt
  or or_2 (or_2_out[0], comparator_4_eq, comparator_5_eq);
  Multiplexer #(.select(2)) multiplexer_2 (.in0(1'b0), .in1(1'b1), .in2(1'b0), .in3(1'b0), .out(fin), .sel(or_2_out));
  Comparator #(.mode("unsigned"), .width(3)) comparator_5 (
    .a(INSTRUCTION[14:12]), .b(3'b111), .eq(comparator_5_eq));  // open: gt, lt

  // Other names for the same wires on the sheet: op[6:0] = INSTRUCTION[6:0]; func3[2:0] = INSTRUCTION[14:12]
endmodule
