// Logisim project alu.circ as structural Verilog: 1 circuit, main circuit alu
module alu (
  input  [31:0] A,
  input  [31:0] B,
  input  [3:0] ALUSel,
  output [31:0] ALUResult
);

  wire comparator_1_lt, slt2;
  wire [4:0] bit_extender_1_out, bit_extender_2_out, bit_extender_3_out;
  wire [31:0] a0, a1, a2, a4, a5, a6, a7, a8, a9, a11, a12, a13, a15, add0, and7, b0, b1, b2, b4, b5, b6, b7,
       b8, b9, b11, b12, b13, b15, bit_extender_4_out, mul8, mulh9, mulhu11, or6, sll1, sra13, srl5, sub12,
       xor4;

  Adder #(.width(32)) adder_1 (.a(a0), .b(b0), .out(add0));  // open: cin, cout
  Shifter #(.width(32)) shifter_1 (.in(a1), .\dist (bit_extender_1_out), .out(sll1));
  Bit_Extender #(.in_width(32), .out_width(5), .\type ("zero")) bit_extender_1 (.in(b1), .out(bit_extender_1_out));
  Multiplexer multiplexer_1 (.in0(1'b0), .in1(comparator_1_lt), .out(slt2), .sel(comparator_1_lt));
  Comparator #(.width(32)) comparator_1 (.a(a2), .b(b2), .lt(comparator_1_lt));  // open: gt, eq
  assign xor4 = a4 ^ b4;  // XOR_Gate xor_1, 32 bits wide
  Demultiplexer #(.select(4), .width(32)) demultiplexer_1 (
    .out0(b0), .out1(b1), .out2(b2), .out4(b4), .out5(b5), .out6(b6), .out7(b7), .out8(b8), .out9(b9),
    .out11(b11), .out12(b12), .out13(b13), .out15(b15), .in(B), .sel(ALUSel));  // open: out3, out10, out14
  Bit_Extender #(.in_width(32), .out_width(5), .\type ("zero")) bit_extender_2 (.in(b5), .out(bit_extender_2_out));
  assign or6 = a6 | b6;  // OR_Gate or_1, 32 bits wide
  assign and7 = a7 & b7;  // AND_Gate and_1, 32 bits wide
  Multiplier #(.mode("twosComplement"), .width(32)) multiplier_1 (.a(a8), .b(b8), .out(mul8));  // open: cin, cout
  Shifter #(.shift("lr"), .width(32)) shifter_2 (.in(a5), .\dist (bit_extender_2_out), .out(srl5));
  Multiplier #(.mode("twosComplement"), .width(32)) multiplier_2 (.a(a9), .b(b9), .cout(mulh9));  // open: out, cin
  Multiplier #(.width(32)) multiplier_3 (.a(a11), .b(b11), .cout(mulhu11));  // open: out, cin
  Subtractor #(.width(32)) subtractor_1 (.a(a12), .b(b12), .out(sub12));  // open: bin, bout
  Bit_Extender #(.in_width(32), .out_width(5), .\type ("zero")) bit_extender_3 (.in(b13), .out(bit_extender_3_out));
  Shifter #(.shift("ar"), .width(32)) shifter_3 (.in(a13), .\dist (bit_extender_3_out), .out(sra13));
  Demultiplexer #(.select(4), .width(32)) demultiplexer_2 (
    .out0(a0), .out1(a1), .out2(a2), .out4(a4), .out5(a5), .out6(a6), .out7(a7), .out8(a8), .out9(a9),
    .out11(a11), .out12(a12), .out13(a13), .out15(a15), .in(A), .sel(ALUSel));  // open: out3, out10, out14
  assign bit_extender_4_out = {{31{1'b0}}, slt2};  // Bit_Extender bit_extender_4
  Multiplexer #(.select(4), .width(32)) multiplexer_2 (
    .in0(add0), .in1(sll1), .in2(bit_extender_4_out), .in4(xor4), .in5(srl5), .in6(or6), .in7(and7),
    .in8(mul8), .in9(mulh9), .in11(mulhu11), .in12(sub12), .in13(sra13), .in15(b15), .out(ALUResult),
    .sel(ALUSel));  // open: in3, in10, in14

  // Other names for the same wires on the sheet: bsel15[31:0] = b15

  // Notes on the sheet:
  //   INPUTS to your circuit
  //   DON'T CHANGE THE LOCATIONS OF THE INPUTS AND OUTPUTS!
  //   OUTPUT from your circuit
endmodule
