// Logisim project control-logic.circ as structural Verilog: 1 circuit, main circuit control_logic
module control_logic (
  input  [31:0] Instruction,
  input  BrEq,
  input  BrLt,
  output PCSel,
  output RegWEn,
  output [2:0] ImmSel,
  output BrUn,
  output ASel,
  output BSel,
  output [3:0] ALUSel,
  output MemWEn,
  output [1:0] WBSel
);

  wire beq_out, bge_out, bgeu_out, blt_out, bltu_out, bne_out, comparator_1_eq, comparator_2_eq,
       comparator_3_eq, comparator_4_eq, comparator_5_eq, comparator_6_eq, comparator_7_eq, comparator_8_eq,
       comparator_9_eq, comparator_10_eq, comparator_11_eq, comparator_12_eq, comparator_13_eq,
       comparator_14_eq, comparator_16_eq, comparator_17_eq, comparator_18_eq, comparator_19_eq,
       comparator_20_eq, comparator_21_eq, comparator_22_eq, comparator_23_eq, comparator_24_eq,
       comparator_25_eq, comparator_26_eq, comparator_29_eq, comparator_30_eq, comparator_31_eq,
       comparator_32_eq, comparator_33_eq, comparator_34_eq, comparator_35_eq, comparator_36_eq,
       comparator_37_eq, comparator_38_eq, comparator_39_eq, comparator_40_eq, comparator_41_eq,
       comparator_42_eq, comparator_43_eq, comparator_44_eq, comparator_45_eq, comparator_46_eq,
       comparator_47_eq, ImmSel_SB, ImmSel_U, ImmSel_UJ, ismul, ismulh, ismulhu, issra, issub, not_1_out,
       not_2_out, not_3_out, or_1_out, or_2_out, or_3_out, or_5_out, or_8_out, or_9_out;
  wire [1:0] multiplexer_12_out;
  wire [2:0] multiplexer_8_out, multiplexer_9_out, multiplexer_10_out;
  wire [3:0] bit_extender_1_out, multiplexer_1_out, multiplexer_2_out, multiplexer_3_out, multiplexer_4_out,
       multiplexer_6_out, multiplexer_7_out;
  wire [15:0] rom_1_data;

  Comparator #(.width(7)) comparator_1 (.a(Instruction[31:25]), .b(7'b0000001), .eq(comparator_1_eq));  // open: gt, lt
  Comparator #(.width(3)) comparator_2 (.a(Instruction[14:12]), .b(3'b000), .eq(comparator_2_eq));  // open: gt, lt
  Comparator #(.width(3)) comparator_3 (.a(Instruction[14:12]), .b(3'b001), .eq(comparator_3_eq));  // open: gt, lt
  Comparator #(.width(3)) comparator_4 (.a(Instruction[14:12]), .b(3'b011), .eq(comparator_4_eq));  // open: gt, lt
  Comparator #(.width(7)) comparator_5 (.a(Instruction[6:0]), .b(7'b0110011), .eq(comparator_5_eq));  // open: gt, lt
  Comparator #(.width(7)) comparator_6 (.a(Instruction[31:25]), .b(7'b0100000), .eq(comparator_6_eq));  // open: gt, lt
  Comparator #(.width(3)) comparator_7 (.a(Instruction[14:12]), .b(3'b000), .eq(comparator_7_eq));  // open: gt, lt
  Comparator #(.width(3)) comparator_8 (.a(Instruction[14:12]), .b(3'b101), .eq(comparator_8_eq));  // open: gt, lt
  Comparator #(.width(7)) comparator_9 (.a(Instruction[31:25]), .b(7'b0100000), .eq(comparator_9_eq));  // open: gt, lt
  Comparator #(.width(7)) comparator_10 (.a(Instruction[6:0]), .b(7'b0110011), .eq(comparator_10_eq));  // open: gt, lt
  Comparator #(.width(7)) comparator_11 (.a(Instruction[6:0]), .b(7'b0010011), .eq(comparator_11_eq));  // open: gt, lt
  and and_1 (ismul, comparator_1_eq, comparator_5_eq, comparator_2_eq);
  and and_2 (ismulh, comparator_1_eq, comparator_3_eq, comparator_5_eq);
  and and_3 (ismulhu, comparator_4_eq, comparator_1_eq, comparator_5_eq);
  and and_4 (issub, comparator_5_eq, comparator_6_eq, comparator_7_eq);
  and and_5 (issra, comparator_8_eq, or_1_out, comparator_9_eq);
  or or_1 (or_1_out, comparator_10_eq, comparator_11_eq);
  ROM #(.addrWidth(6), .dataWidth(16)) rom_1 (.data(rom_1_data));  // open: addr
  assign bit_extender_1_out = {{1{1'b0}}, Instruction[14:12]};  // Bit_Extender bit_extender_1
  Multiplexer #(.width(4)) multiplexer_1 (
    .in0(bit_extender_1_out), .in1(4'b1000), .out(multiplexer_1_out), .sel(ismul));
  Multiplexer #(.width(4)) multiplexer_2 (
    .in0(multiplexer_1_out), .in1(4'b1001), .out(multiplexer_2_out), .sel(ismulh));
  Comparator #(.width(7)) comparator_12 (.a(Instruction[6:0]), .b(7'b0010011), .eq(comparator_12_eq));  // open: gt, lt
  Comparator #(.width(7)) comparator_13 (.a(Instruction[6:0]), .b(7'b0110011), .eq(comparator_13_eq));  // open: gt, lt
  Comparator #(.width(7)) comparator_14 (.a(Instruction[6:0]), .b(7'b0110111), .eq(comparator_14_eq));  // open: gt, lt
  Multiplexer #(.width(4)) multiplexer_3 (
    .in0(multiplexer_2_out), .in1(4'b1011), .out(multiplexer_3_out), .sel(ismulhu));
  or or_2 (or_2_out, comparator_12_eq, comparator_13_eq);
  Multiplexer #(.width(4)) multiplexer_4 (
    .in0(4'b0000), .in1(multiplexer_7_out), .out(multiplexer_4_out), .sel(or_2_out));
  Multiplexer #(.width(4)) multiplexer_5 (.in0(multiplexer_4_out), .in1(4'b1111), .out(ALUSel), .sel(comparator_14_eq));
  Multiplexer #(.width(4)) multiplexer_6 (.in0(multiplexer_3_out), .in1(4'b1100), .out(multiplexer_6_out), .sel(issub));
  Multiplexer #(.width(4)) multiplexer_7 (.in0(multiplexer_6_out), .in1(4'b1101), .out(multiplexer_7_out), .sel(issra));
  Comparator #(.width(7)) comparator_15 (.a(Instruction[6:0]), .b(7'b1100011), .eq(ImmSel_SB));  // open: gt, lt
  Comparator #(.width(3)) comparator_16 (.a(Instruction[14:12]), .b(3'b110), .eq(comparator_16_eq));  // open: gt, lt
  Comparator #(.width(3)) comparator_17 (.a(Instruction[14:12]), .b(3'b111), .eq(comparator_17_eq));  // open: gt, lt
  Comparator #(.width(7)) comparator_18 (.a(Instruction[6:0]), .b(7'b0010111), .eq(comparator_18_eq));  // open: gt, lt
  Comparator #(.width(7)) comparator_19 (.a(Instruction[6:0]), .b(7'b0110111), .eq(comparator_19_eq));  // open: gt, lt
  Multiplexer #(.width(3)) multiplexer_8 (.in0(3'b000), .in1(3'b001), .out(multiplexer_8_out), .sel(MemWEn));
  or or_3 (or_3_out, comparator_16_eq, comparator_17_eq);
  Multiplexer #(.width(3)) multiplexer_9 (
    .in0(multiplexer_8_out), .in1(3'b010), .out(multiplexer_9_out), .sel(ImmSel_SB));
  Comparator #(.width(7)) comparator_20 (.a(Instruction[6:0]), .b(7'b1100011), .eq(comparator_20_eq));  // open: gt, lt
  Comparator #(.width(3)) comparator_21 (.a(Instruction[14:12]), .b(3'b000), .eq(comparator_21_eq));  // open: gt, lt
  Comparator #(.width(3)) comparator_22 (.a(Instruction[14:12]), .b(3'b001), .eq(comparator_22_eq));  // open: gt, lt
  Comparator #(.width(3)) comparator_23 (.a(Instruction[14:12]), .b(3'b100), .eq(comparator_23_eq));  // open: gt, lt
  Comparator #(.width(3)) comparator_24 (.a(Instruction[14:12]), .b(3'b101), .eq(comparator_24_eq));  // open: gt, lt
  Comparator #(.width(3)) comparator_25 (.a(Instruction[14:12]), .b(3'b110), .eq(comparator_25_eq));  // open: gt, lt
  Comparator #(.width(3)) comparator_26 (.a(Instruction[14:12]), .b(3'b111), .eq(comparator_26_eq));  // open: gt, lt
  and and_6 (BrUn, ImmSel_SB, or_3_out);
  or or_4 (ImmSel_U, comparator_18_eq, comparator_19_eq);
  Multiplexer #(.width(3)) multiplexer_10 (
    .in0(multiplexer_9_out), .in1(3'b011), .out(multiplexer_10_out), .sel(ImmSel_U));
  not not_1 (not_1_out, BrEq);
  not not_2 (not_2_out, BrLt);
  not not_3 (not_3_out, BrLt);
  Multiplexer #(.width(3)) multiplexer_11 (.in0(multiplexer_10_out), .in1(3'b100), .out(ImmSel), .sel(ImmSel_UJ));
  and beq (beq_out, comparator_20_eq, comparator_21_eq, BrEq);
  and bne (bne_out, not_1_out, comparator_22_eq, comparator_20_eq);
  and blt (blt_out, comparator_20_eq, comparator_23_eq, BrLt);
  and bge (bge_out, not_2_out, comparator_24_eq, comparator_20_eq);
  and bltu (bltu_out, comparator_20_eq, comparator_25_eq, BrLt);
  and bgeu (bgeu_out, not_3_out, comparator_26_eq, comparator_20_eq);
  Comparator #(.width(7)) comparator_27 (.a(Instruction[6:0]), .b(7'b1101111), .eq(ImmSel_UJ));  // open: gt, lt
  Comparator #(.width(7)) comparator_28 (.a(Instruction[6:0]), .b(7'b0100011), .eq(MemWEn));  // open: gt, lt
  Comparator #(.width(7)) comparator_29 (.a(Instruction[6:0]), .b(7'b1101111), .eq(comparator_29_eq));  // open: gt, lt
  Comparator #(.width(7)) comparator_30 (.a(Instruction[6:0]), .b(7'b0010111), .eq(comparator_30_eq));  // open: gt, lt
  or or_5 (or_5_out, beq_out, bne_out, blt_out, bge_out, bltu_out, bgeu_out);
  Comparator #(.width(7)) comparator_31 (.a(Instruction[6:0]), .b(7'b1101111), .eq(comparator_31_eq));  // open: gt, lt
  Comparator #(.width(7)) comparator_32 (.a(Instruction[6:0]), .b(7'b1100111), .eq(comparator_32_eq));  // open: gt, lt
  or or_6 (ASel, comparator_20_eq, comparator_29_eq, comparator_30_eq);
  or or_7 (PCSel, or_5_out, comparator_31_eq, comparator_32_eq);
  Comparator #(.width(7)) comparator_33 (.a(Instruction[6:0]), .b(7'b0110011), .eq(comparator_33_eq));  // open: gt, lt
  Comparator #(.width(7)) comparator_34 (.a(Instruction[6:0]), .b(7'b0010011), .eq(comparator_34_eq));  // open: gt, lt
  Comparator #(.width(7)) comparator_35 (.a(Instruction[6:0]), .b(7'b0000011), .eq(comparator_35_eq));  // open: gt, lt
  Comparator #(.width(7)) comparator_36 (.a(Instruction[6:0]), .b(7'b0010111), .eq(comparator_36_eq));  // open: gt, lt
  Comparator #(.width(7)) comparator_37 (.a(Instruction[6:0]), .b(7'b0110111), .eq(comparator_37_eq));  // open: gt, lt
  Comparator #(.width(7)) comparator_38 (.a(Instruction[6:0]), .b(7'b1101111), .eq(comparator_38_eq));  // open: gt, lt
  Comparator #(.width(7)) comparator_39 (.a(Instruction[6:0]), .b(7'b1100111), .eq(comparator_39_eq));  // open: gt, lt
  Comparator #(.width(7)) comparator_40 (.a(Instruction[6:0]), .b(7'b1100011), .eq(comparator_40_eq));  // open: gt, lt
  Comparator #(.width(7)) comparator_41 (.a(Instruction[6:0]), .b(7'b0100011), .eq(comparator_41_eq));  // open: gt, lt
  Comparator #(.width(7)) comparator_42 (.a(Instruction[6:0]), .b(7'b0010111), .eq(comparator_42_eq));  // open: gt, lt
  Comparator #(.width(7)) comparator_43 (.a(Instruction[6:0]), .b(7'b0110011), .eq(comparator_43_eq));  // open: gt, lt
  Comparator #(.width(7)) comparator_44 (.a(Instruction[6:0]), .b(7'b0010011), .eq(comparator_44_eq));  // open: gt, lt
  Comparator #(.width(7)) comparator_45 (.a(Instruction[6:0]), .b(7'b0110111), .eq(comparator_45_eq));  // open: gt, lt
  Comparator #(.width(7)) comparator_46 (.a(Instruction[6:0]), .b(7'b1100111), .eq(comparator_46_eq));  // open: gt, lt
  Comparator #(.width(7)) comparator_47 (.a(Instruction[6:0]), .b(7'b1101111), .eq(comparator_47_eq));  // open: gt, lt
  Multiplexer #(.width(2)) multiplexer_12 (.in0(2'b00), .in1(2'b01), .out(multiplexer_12_out), .sel(or_8_out));
  or or_8 (or_8_out, comparator_42_eq, comparator_43_eq, comparator_44_eq, comparator_45_eq);
  or or_9 (or_9_out, comparator_46_eq, comparator_47_eq);
  or or_10 (RegWEn, comparator_33_eq, comparator_34_eq, comparator_35_eq, comparator_36_eq, comparator_37_eq, comparator_38_eq, comparator_39_eq);
  or or_11 (BSel, comparator_39_eq, comparator_38_eq, comparator_37_eq, comparator_36_eq, comparator_35_eq, comparator_34_eq, comparator_40_eq, comparator_41_eq);
  Multiplexer #(.width(2)) multiplexer_13 (.in0(multiplexer_12_out), .in1(2'b10), .out(WBSel), .sel(or_9_out));

  // Other names for the same wires on the sheet: ImmSel_S = MemWEn; opcode[6:0] = Instruction[6:0];
  //   funct3[2:0] = Instruction[14:12]; funct7[6:0] = Instruction[31:25]

  // Notes on the sheet:
  //   INPUTS to your circuit
  //   R
  //   R
  //   R
  //   Connect ROM Input here ->
  //   ROM FOR CONTROL LOGIC
  //   I
  //   R
  //   Lui
  //   DON'T CHANGE THE LOCATIONS OF THE INPUTS AND OUTPUTS!
  //   This is only if you choose to do the ROM option
  //   CONNECT
  //   WIRE
  //   TO
  //   USE
  //   ROM
  //   OUTPUT from your circuit
  //   I
  //   Reminder: If using ROM, use combinational logic for PCSel
  //   SB
  //   Auipc
  //   Lui
  //   B
  //   Jal
  //   S
  //   Jal
  //   Jal
  //   Jalr
  //   Auipc
  //   R
  //   I
  //   Load
  //   Auipc
  //   Lui
  //   Jal
  //   Jalr
  //   B
  //   Store
  //   Auipc
  //   R
  //   I
  //   Lui
  //   Jalr
  //   Jal
  //   Load
  //   ALU
  //   PC + 4
endmodule
