// Logisim project imm-gen.circ as structural Verilog: 1 circuit, main circuit imm_gen
module imm_gen (
  input  [31:0] Instruction,
  input  [2:0] ImmSel,
  output [31:0] Immediate
);

  wire [11:0] Instruction_U;
  wire [31:0] Imm_I, Imm_S, Imm_SB, Imm_UJ, Instruction_I, Instruction_S, Instruction_SB, Instruction_UJ;
  wire [31:12] Imm_U;

  Demultiplexer #(.select(3), .width(32)) demultiplexer_1 (
    .out0(Instruction_I), .out1(Instruction_S), .out2(Instruction_SB), .out3({Imm_U, Instruction_U}),
    .out4(Instruction_UJ), .in(Instruction), .sel(ImmSel));  // open: out5, out6, out7
  assign Imm_I = {{20{Instruction_I[31]}}, Instruction_I[31:20]};  // Bit_Extender bit_extender_1
  assign Imm_S = {{20{Instruction_S[31]}}, {Instruction_S[31:25], Instruction_S[11:7]}};  // Bit_Extender bit_extender_2
  assign Imm_SB = {{19{Instruction_SB[31]}}, {Instruction_SB[31], Instruction_SB[7], Instruction_SB[30:25], Instruction_SB[11:8], 1'b0}};  // Bit_Extender bit_extender_3
  assign Imm_UJ = {{11{Instruction_UJ[31]}}, {Instruction_UJ[31], Instruction_UJ[19:12], Instruction_UJ[20], Instruction_UJ[30:21], 1'b0}};  // Bit_Extender bit_extender_4
  Multiplexer #(.select(3), .width(32)) multiplexer_1 (
    .in0(Imm_I), .in1(Imm_S), .in2(Imm_SB), .in3({Imm_U, {12{1'b0}}}), .in4(Imm_UJ), .out(Immediate),
    .sel(ImmSel));  // open: in5, in6, in7

  // Other names for the same wires on the sheet: Instruction_U[31:12] = Imm_U

  // Notes on the sheet:
  //   INPUTS to your circuit
  //   DON'T CHANGE THE LOCATIONS OF THE INPUTS AND OUTPUTS!
  //   OUTPUT from your circuit
endmodule
