// Logisim project partial-store.circ as structural Verilog: 1 circuit, main circuit partial_store
module partial_store (
  input  [31:0] Instruction,
  input  [31:0] MemAddress,
  input  [31:0] DataFromReg,
  input  MemWEn,
  output [3:0] MemWriteMask,
  output [31:0] DataToMem
);

  wire comparator_1_eq, comparator_2_eq, comparator_3_eq, comparator_4_eq, SB, SH, SW;
  wire [1:0] offset;
  wire [3:0] multiplexer_5_out, multiplexer_6_out, multiplexer_7_out, multiplexer_8_out;
  wire [7:0] bit_extender_2_out;
  wire [15:0] bit_extender_1_out;
  wire [31:0] multiplexer_1_out, multiplexer_2_out, multiplexer_3_out;

  Bit_Extender #(.in_width(32), .\type ("zero")) bit_extender_1 (.in(DataFromReg), .out(bit_extender_1_out));
  Bit_Extender #(.in_width(32), .out_width(8), .\type ("zero")) bit_extender_2 (
    .in(DataFromReg), .out(bit_extender_2_out));
  Multiplexer #(.width(32)) multiplexer_1 (
    .in0(DataFromReg), .in1(multiplexer_2_out), .out(multiplexer_1_out), .sel(SH));
  Multiplexer #(.select(2), .width(32)) multiplexer_2 (
    .in0({{16{1'b0}}, bit_extender_1_out}), .in2({bit_extender_1_out, {16{1'b0}}}), .out(multiplexer_2_out),
    .sel(offset));  // open: in1, in3
  Multiplexer #(.select(2), .width(32)) multiplexer_3 (
    .in0({{24{1'b0}}, bit_extender_2_out}), .in1({{16{1'b0}}, bit_extender_2_out, {8{1'b0}}}),
    .in2({{8{1'b0}}, bit_extender_2_out, {16{1'b0}}}), .in3({bit_extender_2_out, {24{1'b0}}}),
    .out(multiplexer_3_out), .sel(offset));
  Multiplexer #(.width(32)) multiplexer_4 (.in0(multiplexer_1_out), .in1(multiplexer_3_out), .out(DataToMem), .sel(SB));
  Multiplexer #(.select(2), .width(4)) multiplexer_5 (
    .in0(4'b0011), .in2(4'b1100), .out(multiplexer_5_out), .sel(offset));  // open: in1, in3
  Multiplexer #(.width(4)) multiplexer_6 (.in0(4'b1111), .in1(multiplexer_5_out), .out(multiplexer_6_out), .sel(SH));
  Bit_Extender #(.in_width(32), .out_width(2), .\type ("zero")) bit_extender_3 (.in(MemAddress), .out(offset));
  Multiplexer #(.width(4)) multiplexer_7 (
    .in0(multiplexer_6_out), .in1(multiplexer_8_out), .out(multiplexer_7_out), .sel(SB));
  Multiplexer #(.select(2), .width(4)) multiplexer_8 (
    .in0(4'b0001), .in1(4'b0010), .in2(4'b0100), .in3(4'b1000), .out(multiplexer_8_out), .sel(offset));
  Multiplexer #(.width(4)) multiplexer_9 (.in0(4'b0000), .in1(multiplexer_7_out), .out(MemWriteMask), .sel(MemWEn));
  Comparator #(.width(7)) comparator_1 (.a(Instruction[6:0]), .b(7'b0100011), .eq(comparator_1_eq));  // open: gt, lt
  Comparator #(.width(3)) comparator_2 (.a(Instruction[14:12]), .b(3'b000), .eq(comparator_2_eq));  // open: gt, lt
  Comparator #(.width(3)) comparator_3 (.a(Instruction[14:12]), .b(3'b001), .eq(comparator_3_eq));  // open: gt, lt
  Comparator #(.width(3)) comparator_4 (.a(Instruction[14:12]), .b(3'b010), .eq(comparator_4_eq));  // open: gt, lt
  and and_1 (SB, comparator_1_eq, comparator_2_eq);
  and and_2 (SH, comparator_1_eq, comparator_3_eq);
  and and_3 (SW, comparator_1_eq, comparator_4_eq);

  // Other names for the same wires on the sheet: opcode[6:0] = Instruction[6:0]; funct3[2:0] = Instruction[14:12]

  // Notes on the sheet:
  //   INPUTS to your circuit
  //   DON'T CHANGE THE LOCATIONS OF THE INPUTS AND OUTPUTS!
  //   OUTPUT from your circuit
endmodule
