// Logisim project regfile.circ as structural Verilog: 1 circuit, main circuit regfile
module regfile (
  input  [4:0] ReadIndex1,
  input  [4:0] ReadIndex2,
  input  [4:0] WriteIndex,
  input  [31:0] WriteData,
  input  RegWEn,
  input  clk,
  output [31:0] ra,
  output [31:0] sp,
  output [31:0] t0,
  output [31:0] t1,
  output [31:0] t2,
  output [31:0] s0,
  output [31:0] s1,
  output [31:0] a0,
  output [31:0] ReadData1,
  output [31:0] ReadData2
);

  wire i2, i3, i4, i5, i6, i7, i8, i9, i10, i11, i12, i13, i14, i15, i16, i17, i18, i19, i20, i21, i22, i23,
       i24, i25, i26, i27, i28, i29, i30, i31, i32;
  wire [31:0] a1, a2, a3, a4, a5, a6, a7, gp, s2, s3, s4, s5, s6, s7, s8, s9, s10, s11, t3, t4, t5, t6, tp,
       zero;

  Demultiplexer #(.select(5)) demultiplexer_1 (
    .out1(i2), .out2(i3), .out3(i4), .out4(i5), .out5(i6), .out6(i7), .out7(i8), .out8(i9), .out9(i10),
    .out10(i11), .out11(i12), .out12(i13), .out13(i14), .out14(i15), .out15(i16), .out16(i17), .out17(i18),
    .out18(i19), .out19(i20), .out20(i21), .out21(i22), .out22(i23), .out23(i24), .out24(i25), .out25(i26),
    .out26(i27), .out27(i28), .out28(i29), .out29(i30), .out30(i31), .out31(i32), .in(RegWEn),
    .sel(WriteIndex));  // open: out0
  Multiplexer #(.select(5), .width(32)) multiplexer_1 (
    .in0(zero), .in1(ra), .in2(sp), .in3(gp), .in4(tp), .in5(t0), .in6(t1), .in7(t2), .in8(s0), .in9(s1),
    .in10(a0), .in11(a1), .in12(a2), .in13(a3), .in14(a4), .in15(a5), .in16(a6), .in17(a7), .in18(s2),
    .in19(s3), .in20(s4), .in21(s5), .in22(s6), .in23(s7), .in24(s8), .in25(s9), .in26(s10), .in27(s11),
    .in28(t3), .in29(t4), .in30(t5), .in31(t6), .out(ReadData1), .sel(ReadIndex1));
  Multiplexer #(.select(5), .width(32)) multiplexer_2 (
    .in0(zero), .in1(ra), .in2(sp), .in3(gp), .in4(tp), .in5(t0), .in6(t1), .in7(t2), .in8(s0), .in9(s1),
    .in10(a0), .in11(a1), .in12(a2), .in13(a3), .in14(a4), .in15(a5), .in16(a6), .in17(a7), .in18(s2),
    .in19(s3), .in20(s4), .in21(s5), .in22(s6), .in23(s7), .in24(s8), .in25(s9), .in26(s10), .in27(s11),
    .in28(t3), .in29(t4), .in30(t5), .in31(t6), .out(ReadData2), .sel(ReadIndex2));
  Register #(.width(32)) x0 (.en(1'b0), .clk(clk), .Q(zero));  // open: D, clr
  Register #(.width(32)) x8 (.D(WriteData), .en(i9), .clk(clk), .Q(s0));  // open: clr
  Register #(.width(32)) x16 (.D(WriteData), .en(i17), .clk(clk), .Q(a6));  // open: clr
  Register #(.width(32)) x24 (.D(WriteData), .en(i25), .clk(clk), .Q(s8));  // open: clr
  Register #(.width(32)) x1 (.D(WriteData), .en(i2), .clk(clk), .Q(ra));  // open: clr
  Register #(.width(32)) x9 (.D(WriteData), .en(i10), .clk(clk), .Q(s1));  // open: clr
  Register #(.width(32)) x17 (.D(WriteData), .en(i18), .clk(clk), .Q(a7));  // open: clr
  Register #(.width(32)) x25 (.D(WriteData), .en(i26), .clk(clk), .Q(s9));  // open: clr
  Register #(.width(32)) x2 (.D(WriteData), .en(i3), .clk(clk), .Q(sp));  // open: clr
  Register #(.width(32)) x26 (.D(WriteData), .en(i27), .clk(clk), .Q(s10));  // open: clr
  Register #(.width(32)) x10 (.D(WriteData), .en(i11), .clk(clk), .Q(a0));  // open: clr
  Register #(.width(32)) x18 (.D(WriteData), .en(i19), .clk(clk), .Q(s2));  // open: clr
  Register #(.width(32)) x3 (.D(WriteData), .en(i4), .clk(clk), .Q(gp));  // open: clr
  Register #(.width(32)) x11 (.D(WriteData), .en(i12), .clk(clk), .Q(a1));  // open: clr
  Register #(.width(32)) x19 (.D(WriteData), .en(i20), .clk(clk), .Q(s3));  // open: clr
  Register #(.width(32)) x27 (.D(WriteData), .en(i28), .clk(clk), .Q(s11));  // open: clr
  Register #(.width(32)) x4 (.D(WriteData), .en(i5), .clk(clk), .Q(tp));  // open: clr
  Register #(.width(32)) x12 (.D(WriteData), .en(i13), .clk(clk), .Q(a2));  // open: clr
  Register #(.width(32)) x20 (.D(WriteData), .en(i21), .clk(clk), .Q(s4));  // open: clr
  Register #(.width(32)) x28 (.D(WriteData), .en(i29), .clk(clk), .Q(t3));  // open: clr
  Register #(.width(32)) x5 (.D(WriteData), .en(i6), .clk(clk), .Q(t0));  // open: clr
  Register #(.width(32)) x13 (.D(WriteData), .en(i14), .clk(clk), .Q(a3));  // open: clr
  Register #(.width(32)) x21 (.D(WriteData), .en(i22), .clk(clk), .Q(s5));  // open: clr
  Register #(.width(32)) x29 (.D(WriteData), .en(i30), .clk(clk), .Q(t4));  // open: clr
  Register #(.width(32)) x6 (.D(WriteData), .en(i7), .clk(clk), .Q(t1));  // open: clr
  Register #(.width(32)) x14 (.D(WriteData), .en(i15), .clk(clk), .Q(a4));  // open: clr
  Register #(.width(32)) x22 (.D(WriteData), .en(i23), .clk(clk), .Q(s6));  // open: clr
  Register #(.width(32)) x30 (.D(WriteData), .en(i31), .clk(clk), .Q(t5));  // open: clr
  Register #(.width(32)) x7 (.D(WriteData), .en(i8), .clk(clk), .Q(t2));  // open: clr
  Register #(.width(32)) x15 (.D(WriteData), .en(i16), .clk(clk), .Q(a5));  // open: clr
  Register #(.width(32)) x23 (.D(WriteData), .en(i24), .clk(clk), .Q(s7));  // open: clr
  Register #(.width(32)) x31 (.D(WriteData), .en(i32), .clk(clk), .Q(t6));  // open: clr

  // Notes on the sheet:
  //   INPUTS to your circuit
  //   DON'T CHANGE THE LOCATIONS OF THE INPUTS AND OUTPUTS!
  //   These are DEBUG/TEST outputs from your circuit.
  //   OUTPUTS from your circuit
endmodule
